# Fritzing sketch lukiled (saved by Fritzing 1.0.2b)
breadboards: 1

parts:
  Mod1 = seeeduino-xiao
  A1 = w5500 module
  Bauteil1 = NeoPixel Stick [part_number=1426]

nets:
  N1: Mod1.D0, Bauteil1.DATAIN
  N2: Mod1.D4, A1.Pin_5
  N3: Mod1.D8, A1.Pin_4
  N4: Mod1.D9, A1.Pin_7
  N5: Mod1.D10, A1.Pin_3
  N6: Mod1.3V3, A1.Pin_10, A1.Pin_11
  N7: Mod1.GND, A1.Pin_2
  5V: Mod1.5V, Bauteil1.+5V

custom parts:
  seeeduino-xiao: Seeeduino XIAO processor board.
  w5500 module: MELIFE 3pcs W5500 SPI to LAN Ethernet Network Module TCP IP STM32 Interface 3.3V 5V Compatible with WIZ820io RC5.
  NeoPixel Stick: Make your own little LED strip arrangement with this stick of NeoPixel LEDs. We crammed 8 of the tiny 5050 (5mm x 5mm) smart RGB LEDs onto a PCB with mounting holes and a chainable design. Use only one microcontroller pin to control as many as you can chain together! Each LED is addressable as the driver chip is inside the LED. Each one has ~18mA constant current drive so the color will be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
